// Logisim project Final Project Advanced.circ as structural Verilog
module _16_bit_ALU (
  input  [15:0] A,
  input  [15:0] B,
  input  [1:0] ALU_Op,
  output [15:0] out_4
);

  wire and_1_out;
  wire [15:0] adder_1_out, and_2_out, multiplexer_1_out, not_1_out, or_1_out;

  Multiplexer #(.width(16), .enable("false")) multiplexer_1 (
    .in0(B), .in1(not_1_out), .out(multiplexer_1_out), .sel(and_1_out));
  assign not_1_out = ~B;  // NOT_Gate not_1, 16 bits wide
  and and_1 (and_1_out, ALU_Op[0], ALU_Op[1]);
  Adder #(.width(16)) adder_1 (.a(A), .b(multiplexer_1_out), .out(adder_1_out), .cin(and_1_out));  // open: cout
  assign and_2_out = multiplexer_1_out & A;  // AND_Gate and_2, 16 bits wide
  assign or_1_out = multiplexer_1_out | A;  // OR_Gate or_1, 16 bits wide
  Multiplexer #(.select(2), .width(16), .enable("false")) multiplexer_2 (
    .in0(adder_1_out), .in1(and_2_out), .in2(or_1_out), .in3(adder_1_out), .out(out_4), .sel(ALU_Op));

  // Notes on the sheet:
  //   4 Bit ALU
  //   00 = ADD
  //   01 = AND
  //   10 = OR
  //   11 = SUB
  //   sub not B
  //   sub cin
  //   sub
endmodule

module _16_bit_register_file (
  input  [15:0] Data_In,
  input  [2:0] Read_Addr_1,
  input  Write_Enable,
  input  [2:0] Write_Addr,
  input  [2:0] Read_Addr_2,
  input  Clock,
  output [15:0] Read_1_Data,
  output [15:0] Read_2_Data
);

  wire demultiplexer_1_out0, demultiplexer_1_out1, demultiplexer_1_out2, demultiplexer_1_out3,
       demultiplexer_1_out4, demultiplexer_1_out5, demultiplexer_1_out6, demultiplexer_1_out7;
  wire [15:0] register_1_q, register_2_q, register_3_q, register_4_q, register_5_q, register_6_q,
       register_7_q, register_8_q;

  Demultiplexer #(.select(3), .enable("false")) demultiplexer_1 (
    .out0(demultiplexer_1_out0), .out1(demultiplexer_1_out1), .out2(demultiplexer_1_out2),
    .out3(demultiplexer_1_out3), .out4(demultiplexer_1_out4), .out5(demultiplexer_1_out5),
    .out6(demultiplexer_1_out6), .out7(demultiplexer_1_out7), .in(Write_Enable), .sel(Write_Addr));
  Register #(.width(16)) register_1 (
    .D(Data_In), .en(demultiplexer_1_out0), .Q(register_1_q), .clk(Clock));  // open: clr
  Register #(.width(16)) register_2 (
    .D(Data_In), .en(demultiplexer_1_out1), .Q(register_2_q), .clk(Clock));  // open: clr
  Register #(.width(16)) register_3 (
    .D(Data_In), .en(demultiplexer_1_out2), .Q(register_3_q), .clk(Clock));  // open: clr
  Register #(.width(16)) register_4 (
    .D(Data_In), .en(demultiplexer_1_out3), .Q(register_4_q), .clk(Clock));  // open: clr
  Register #(.width(16)) register_5 (
    .D(Data_In), .en(demultiplexer_1_out4), .Q(register_5_q), .clk(Clock));  // open: clr
  Register #(.width(16)) register_6 (
    .D(Data_In), .en(demultiplexer_1_out5), .Q(register_6_q), .clk(Clock));  // open: clr
  Register #(.width(16)) register_7 (
    .D(Data_In), .en(demultiplexer_1_out6), .Q(register_7_q), .clk(Clock));  // open: clr
  Register #(.width(16)) register_8 (
    .D(Data_In), .en(demultiplexer_1_out7), .Q(register_8_q), .clk(Clock));  // open: clr
  Multiplexer #(.select(3), .width(16), .enable("false")) multiplexer_1 (
    .in0(register_1_q), .in1(register_2_q), .in2(register_3_q), .in3(register_4_q), .in4(register_5_q),
    .in5(register_6_q), .in6(register_7_q), .in7(register_8_q), .out(Read_1_Data), .sel(Read_Addr_1));
  Multiplexer #(.select(3), .width(16), .enable("false")) multiplexer_2 (
    .in0(register_1_q), .in1(register_2_q), .in2(register_3_q), .in3(register_4_q), .in4(register_5_q),
    .in5(register_6_q), .in6(register_7_q), .in7(register_8_q), .out(Read_2_Data), .sel(Read_Addr_2));

  // Notes on the sheet:
  //   8x4-bit Register File
endmodule

module Basic_16_bit_processor (
  input  clock
);

  wire and_1_out, comparator_1_eq, control_logic_1_beq, control_logic_1_immediate, control_logic_1_jump,
       control_logic_1_lw, control_logic_1_sw, control_logic_1_sw_mux, control_logic_1_we, not_1_out,
       not_2_out;
  wire [1:0] control_logic_1_alu_op;
  wire [2:0] demultiplexer_2_out0, multiplexer_3_out;
  wire [8:0] adder_1_out, bit_extender_1_out, demultiplexer_1_out0, multiplexer_1_out, multiplexer_2_out,
       register_1_q;
  wire [13:0] rom_1_data;
  wire [15:0] bit_extender_2_out, multiplexer_4_out, multiplexer_5_out, n16_bit_alu_1_out_4,
       n16_bit_register_file_1_read_1_data, n16_bit_register_file_1_read_2_data, ram_1_data;

  assign bit_extender_1_out = {{6{demultiplexer_2_out0[2]}}, demultiplexer_2_out0};  // Bit_Extender bit_extender_1
  Multiplexer #(.width(9), .enable("false")) multiplexer_1 (
    .in0(9'h1), .in1(bit_extender_1_out), .out(multiplexer_1_out), .sel(and_1_out));
  Adder #(.width(9)) adder_1 (.a(register_1_q), .b(multiplexer_1_out), .out(adder_1_out));  // open: cin, cout
  Multiplexer #(.width(9), .enable("false")) multiplexer_2 (
    .in0(adder_1_out), .in1(demultiplexer_1_out0), .out(multiplexer_2_out), .sel(control_logic_1_jump));
  Register #(.width(9)) register_1 (.D(multiplexer_2_out), .Q(register_1_q), .clk(clock));  // open: en, clr
  ROM #(.addrWidth(9), .dataWidth(14)) rom_1 (.addr(register_1_q), .data(rom_1_data));  // open: sel
  Control_logic control_logic_1 (
    .in_1(rom_1_data[13:9]), .SW_Mux(control_logic_1_sw_mux), .WE(control_logic_1_we),
    .ALU_op(control_logic_1_alu_op), .Immediate(control_logic_1_immediate), .SW(control_logic_1_sw),
    .LW(control_logic_1_lw), .Beq(control_logic_1_beq), .Jump(control_logic_1_jump));
  Demultiplexer #(.width(9)) demultiplexer_1 (
    .out0(demultiplexer_1_out0), .in(rom_1_data[8:0]), .sel(not_1_out), .en(control_logic_1_jump));  // open: out1
  not not_1 (not_1_out, control_logic_1_jump);
  Multiplexer #(.width(3), .enable("false")) multiplexer_3 (
    .in0(rom_1_data[2:0]), .in1(rom_1_data[8:6]), .out(multiplexer_3_out), .sel(control_logic_1_sw_mux));
  _16_bit_register_file u_16_bit_register_file_1 (
    .Data_In(multiplexer_4_out), .Write_Enable(control_logic_1_we), .Clock(clock),
    .Write_Addr(rom_1_data[8:6]), .Read_Addr_1(rom_1_data[5:3]), .Read_Addr_2(multiplexer_3_out),
    .Read_1_Data(n16_bit_register_file_1_read_1_data), .Read_2_Data(n16_bit_register_file_1_read_2_data));
  assign bit_extender_2_out = {{13{rom_1_data[2]}}, rom_1_data[2:0]};  // Bit_Extender bit_extender_2
  Multiplexer #(.width(16), .enable("false")) multiplexer_4 (
    .in0(n16_bit_alu_1_out_4), .in1(ram_1_data), .out(multiplexer_4_out), .sel(control_logic_1_lw));
  _16_bit_ALU u_16_bit_alu_1 (
    .A(n16_bit_register_file_1_read_1_data), .B(multiplexer_5_out), .ALU_Op(control_logic_1_alu_op),
    .out_4(n16_bit_alu_1_out_4));
  Multiplexer #(.width(16), .enable("false")) multiplexer_5 (
    .in0(n16_bit_register_file_1_read_2_data), .in1(bit_extender_2_out), .out(multiplexer_5_out),
    .sel(control_logic_1_immediate));
  Comparator #(.width(3)) comparator_1 (
    .a(rom_1_data[8:6]), .b(rom_1_data[5:3]), .eq(comparator_1_eq));  // open: gt, lt
  and and_1 (and_1_out, control_logic_1_beq, comparator_1_eq);
  RAM #(.addrWidth(16), .dataWidth(16), .bus("separate")) ram_1 (
    .addr(n16_bit_alu_1_out_4), .din(n16_bit_register_file_1_read_2_data), .data(ram_1_data),
    .str(control_logic_1_sw), .clk(clock), .ld(control_logic_1_lw));  // open: sel, clr
  Demultiplexer #(.width(3)) demultiplexer_2 (
    .out0(demultiplexer_2_out0), .in(rom_1_data[2:0]), .sel(not_2_out), .en(and_1_out));  // open: out1
  not not_2 (not_2_out, and_1_out);

  // Notes on the sheet:
  //   contents of rom_1 (hex, n*v repeats v):
  //   201 100a 124a 14df
  //   op
  //   src2
  //   dest
  //   src1
  //   immed data
  //   src2
  //   ALU op
endmodule

module Control_logic (
  input  [4:0] in_1,
  output SW_Mux,
  output WE,
  output [1:0] ALU_op,
  output Immediate,
  output SW,
  output LW,
  output Beq,
  output Jump
);

  ROM #(.addrWidth(5)) rom_1 (.addr(in_1), .data({ALU_op, WE, Immediate, SW, LW, Beq, Jump}));  // open: sel

  assign SW_Mux = SW;

  // Notes on the sheet:
  //   contents of rom_1 (hex, n*v repeats v):
  //   20 30 60 70 a0 b0 e0 f0 18 24 2 1
endmodule
