// Logisim project Final Project Basic.circ as structural Verilog
module _16_bit_ALU (
  input  [15:0] A,
  input  [15:0] B,
  input  [1:0] ALU_Op,
  output [15:0] out_4
);

  wire and_1_out;
  wire [15:0] adder_1_out, and_2_out, multiplexer_1_out, not_1_out, or_1_out;

  Multiplexer #(.width(16), .enable("false")) multiplexer_1 (
    .in0(B), .in1(not_1_out), .out(multiplexer_1_out), .sel(and_1_out));
  assign not_1_out = ~B;  // NOT_Gate not_1, 16 bits wide
  and and_1 (and_1_out, ALU_Op[0], ALU_Op[1]);
  Adder #(.width(16)) adder_1 (.a(A), .b(multiplexer_1_out), .out(adder_1_out), .cin(and_1_out));  // open: cout
  assign and_2_out = multiplexer_1_out & A;  // AND_Gate and_2, 16 bits wide
  assign or_1_out = multiplexer_1_out | A;  // OR_Gate or_1, 16 bits wide
  Multiplexer #(.select(2), .width(16), .enable("false")) multiplexer_2 (
    .in0(adder_1_out), .in1(and_2_out), .in2(or_1_out), .in3(adder_1_out), .out(out_4), .sel(ALU_Op));

  // Notes on the sheet:
  //   4 Bit ALU
  //   00 = ADD
  //   01 = AND
  //   10 = OR
  //   11 = SUB
  //   sub not B
  //   sub cin
  //   sub
endmodule

module _16_bit_register_file (
  input  [15:0] Data_In,
  input  [2:0] Read_Addr_1,
  input  Write_Enable,
  input  [2:0] Write_Addr,
  input  [2:0] Read_Addr_2,
  input  Clock,
  output [15:0] Read_1_Data,
  output [15:0] Read_2_Data
);

  wire demultiplexer_1_out0, demultiplexer_1_out1, demultiplexer_1_out2, demultiplexer_1_out3,
       demultiplexer_1_out4, demultiplexer_1_out5, demultiplexer_1_out6, demultiplexer_1_out7;
  wire [15:0] register_1_q, register_2_q, register_3_q, register_4_q, register_5_q, register_6_q,
       register_7_q, register_8_q;

  Demultiplexer #(.select(3), .enable("false")) demultiplexer_1 (
    .out0(demultiplexer_1_out0), .out1(demultiplexer_1_out1), .out2(demultiplexer_1_out2),
    .out3(demultiplexer_1_out3), .out4(demultiplexer_1_out4), .out5(demultiplexer_1_out5),
    .out6(demultiplexer_1_out6), .out7(demultiplexer_1_out7), .in(Write_Enable), .sel(Write_Addr));
  Register #(.width(16)) register_1 (
    .D(Data_In), .en(demultiplexer_1_out0), .Q(register_1_q), .clk(Clock));  // open: clr
  Register #(.width(16)) register_2 (
    .D(Data_In), .en(demultiplexer_1_out1), .Q(register_2_q), .clk(Clock));  // open: clr
  Register #(.width(16)) register_3 (
    .D(Data_In), .en(demultiplexer_1_out2), .Q(register_3_q), .clk(Clock));  // open: clr
  Register #(.width(16)) register_4 (
    .D(Data_In), .en(demultiplexer_1_out3), .Q(register_4_q), .clk(Clock));  // open: clr
  Register #(.width(16)) register_5 (
    .D(Data_In), .en(demultiplexer_1_out4), .Q(register_5_q), .clk(Clock));  // open: clr
  Register #(.width(16)) register_6 (
    .D(Data_In), .en(demultiplexer_1_out5), .Q(register_6_q), .clk(Clock));  // open: clr
  Register #(.width(16)) register_7 (
    .D(Data_In), .en(demultiplexer_1_out6), .Q(register_7_q), .clk(Clock));  // open: clr
  Register #(.width(16)) register_8 (
    .D(Data_In), .en(demultiplexer_1_out7), .Q(register_8_q), .clk(Clock));  // open: clr
  Multiplexer #(.select(3), .width(16), .enable("false")) multiplexer_1 (
    .in0(register_1_q), .in1(register_2_q), .in2(register_3_q), .in3(register_4_q), .in4(register_5_q),
    .in5(register_6_q), .in6(register_7_q), .in7(register_8_q), .out(Read_1_Data), .sel(Read_Addr_1));
  Multiplexer #(.select(3), .width(16), .enable("false")) multiplexer_2 (
    .in0(register_1_q), .in1(register_2_q), .in2(register_3_q), .in3(register_4_q), .in4(register_5_q),
    .in5(register_6_q), .in6(register_7_q), .in7(register_8_q), .out(Read_2_Data), .sel(Read_Addr_2));

  // Notes on the sheet:
  //   8x4-bit Register File
endmodule

module Basic_16_bit_processor (
  input  clock
);

  wire control_logic_1_imm, control_logic_1_lw, control_logic_1_lw_select, control_logic_1_mux_sw,
       control_logic_1_sw, control_logic_1_we_sw;
  wire [1:0] control_logic_1_op;
  wire [2:0] multiplexer_1_out;
  wire [8:0] adder_1_out, counter_1_q;
  wire [13:0] rom_1_data;
  wire [15:0] bit_extender_1_out, multiplexer_2_out, multiplexer_3_out, n16_bit_alu_1_out_4,
       n16_bit_register_file_1_read_1_data, n16_bit_register_file_1_read_2_data, ram_1_data;

  Adder #(.width(9)) adder_1 (.a(counter_1_q), .b(9'h1), .out(adder_1_out));  // open: cin, cout
  Counter #(.width(9), .max('h1ff)) counter_1 (
    .D(adder_1_out), .Q(counter_1_q), .clk(clock));  // open: load, count, carry, clr
  ROM #(.addrWidth(9), .dataWidth(14)) rom_1 (.addr(counter_1_q), .data(rom_1_data));  // open: sel
  Control_logic control_logic_1 (
    .in_1(rom_1_data[13:9]), .LW_select(control_logic_1_lw_select), .WE_SW(control_logic_1_we_sw),
    .MUX_SW(control_logic_1_mux_sw), .IMM(control_logic_1_imm), .LW(control_logic_1_lw),
    .SW(control_logic_1_sw), .Op(control_logic_1_op));
  _16_bit_register_file u_16_bit_register_file_1 (
    .Data_In(multiplexer_2_out), .Write_Enable(control_logic_1_we_sw), .Clock(clock),
    .Write_Addr(rom_1_data[8:6]), .Read_Addr_1(rom_1_data[5:3]), .Read_Addr_2(multiplexer_1_out),
    .Read_1_Data(n16_bit_register_file_1_read_1_data), .Read_2_Data(n16_bit_register_file_1_read_2_data));
  Multiplexer #(.width(3), .enable("false")) multiplexer_1 (
    .in0(rom_1_data[2:0]), .in1(rom_1_data[8:6]), .out(multiplexer_1_out), .sel(control_logic_1_mux_sw));
  assign bit_extender_1_out = {{13{rom_1_data[2]}}, rom_1_data[2:0]};  // Bit_Extender bit_extender_1
  Multiplexer #(.width(16), .enable("false")) multiplexer_2 (
    .in0(n16_bit_alu_1_out_4), .in1(ram_1_data), .out(multiplexer_2_out), .sel(control_logic_1_lw_select));
  Multiplexer #(.width(16), .enable("false")) multiplexer_3 (
    .in0(n16_bit_register_file_1_read_2_data), .in1(bit_extender_1_out), .out(multiplexer_3_out),
    .sel(control_logic_1_imm));
  _16_bit_ALU u_16_bit_alu_1 (
    .A(n16_bit_register_file_1_read_1_data), .B(multiplexer_3_out), .ALU_Op(control_logic_1_op),
    .out_4(n16_bit_alu_1_out_4));
  RAM #(.addrWidth(16), .dataWidth(16), .bus("separate")) ram_1 (
    .addr(n16_bit_alu_1_out_4), .din(n16_bit_register_file_1_read_2_data), .data(ram_1_data),
    .str(control_logic_1_sw), .clk(clock), .ld(control_logic_1_lw));  // open: sel, clr

  // Notes on the sheet:
  //   contents of rom_1 (hex, n*v repeats v):
  //   10 9a 601 2603 2810 2602 2501 320 56d 56c 2568 3090 295c 2007 3004 205 2848 3048 49 8
  //   op
  //   src2
  //   ALU op
  //   dest
  //   src1
  //   immed data
endmodule

module Control_logic (
  input  [4:0] in_1,
  output LW_select,
  output WE_SW,
  output MUX_SW,
  output IMM,
  output LW,
  output SW,
  output [1:0] Op
);

  not not_1 (WE_SW, in_1[2]);

  assign IMM = in_1[4];
  assign LW = in_1[3];
  assign LW_select = in_1[3];
  assign MUX_SW = in_1[2];
  assign Op = in_1[1:0];
  assign SW = in_1[2];
endmodule
